# Fritzing sketch esplightstick (saved by Fritzing 0.9.3b)
perfboards: 2

parts:
  S5 = Pushbutton [package="[THT]"]
  WeMos_D1_Mini_OLED_Shield1 = WeMos D1 Mini Micro SD Shield
  WeMos_D1_Mini_OLED_Shield2 = WeMos D1 Mini OLED Shield
  NEOPIXEL2 = Neopixel Strip -- Black (60/m) [part_number=1461]
  J3 = JST-B3P-VH [part_number=JST-B3P-VH package=THT]
  J4 = JST-VHR-3N [part_number=JST-VHR-3N package=THT]
  S3 = Pushbutton [package="[THT]"]
  S2 = Pushbutton [package="[THT]"]
  S1 = Pushbutton [package="[THT]"]
  R1 = Resistor [tolerance=±5% resistance=2.2k package=THT]
  R2 = Resistor [tolerance=±5% resistance=330 package=THT]
  R5 = Resistor [tolerance=±5% resistance=1k package=THT]
  R4 = Resistor [tolerance=±5% resistance=3.3k package=THT]
  S4 = Pushbutton [package="[THT]"]
  R3 = Resistor [tolerance=±5% resistance=470 package=THT]
  C2 = Electrolytic Capacitor [capacitance=10μF voltage=35V package="0605 [SMD, electrolytic]"]
  U1 = Voltage Regulator - 5V [package="TO220 [THT]"]
  C3 = Electrolytic Capacitor [capacitance=10μF voltage=35V package="0605 [SMD, electrolytic]"]
  BAT1 = Battery Holders [package=battery-aa]
  J10 = Power Plug
  J11 = Power Jack [package=power_jack_slot]
  S6 = SPST Switch [package=switch-spdt_kit]
  BAT2 = Battery Holders [package=battery-aa]
  BAT3 = Battery Holders [package=battery-aa]
  BAT4 = Battery Holders [package=battery-aa]  # not connected
  BAT5 = Battery Holders [package=battery-aa]
  BAT6 = Battery Holders [package=battery-aa]
  BAT7 = Battery Holders [package=battery-aa]
  WeMos_D1_Mini1 = WeMos D1 Mini
  S8 = Pushbutton [part_number=COM-09190 package="[THT]"]
  R6 = Resistor [tolerance=±5% resistance=470 package=THT]

nets (from the breadboard view):
  N1: S5.Pin_1, S5.Pin_2
  GND: S5.Pin_3, S5.Pin_4, WeMos_D1_Mini_OLED_Shield1.A0, WeMos_D1_Mini_OLED_Shield1.G, WeMos_D1_Mini_OLED_Shield2.A0, WeMos_D1_Mini_OLED_Shield2.G, J3.pin1, S3.Pin_3, S3.Pin_4, S2.Pin_3, S2.Pin_4, S1.Pin_3, S1.Pin_4, R1.Pin_0, R2.Pin_0, R2.Pin_1, R5.Pin_0, R5.Pin_1, R4.Pin_0, R4.Pin_1, R3.Pin_1, C2.-, U1.GND, C3.-, J10.GND, J10.tip_GND, J11.GND, J11.tip_GND, BAT7.+, WeMos_D1_Mini1.A0
  3V3: WeMos_D1_Mini_OLED_Shield1.3V3, WeMos_D1_Mini_OLED_Shield2.3V3, WeMos_D1_Mini1.3V3
  5V: WeMos_D1_Mini_OLED_Shield1.5V, WeMos_D1_Mini_OLED_Shield2.5V, J3.pin3, U1.output_voltage, C3.+, WeMos_D1_Mini1.5V
  N2: WeMos_D1_Mini_OLED_Shield1.D0, WeMos_D1_Mini_OLED_Shield2.D0, WeMos_D1_Mini1.D0, R6.Pin_0
  N3: WeMos_D1_Mini_OLED_Shield1.D1, WeMos_D1_Mini_OLED_Shield2.D1, WeMos_D1_Mini1.D1
  N4: WeMos_D1_Mini_OLED_Shield1.D2, WeMos_D1_Mini_OLED_Shield2.D2, WeMos_D1_Mini1.D2
  N5: WeMos_D1_Mini_OLED_Shield1.D3, WeMos_D1_Mini_OLED_Shield2.D3, WeMos_D1_Mini1.D3
  N6: WeMos_D1_Mini_OLED_Shield1.D4, WeMos_D1_Mini_OLED_Shield2.D4, WeMos_D1_Mini1.D4
  N7: WeMos_D1_Mini_OLED_Shield1.D5, WeMos_D1_Mini_OLED_Shield2.D5, WeMos_D1_Mini1.D5
  N8: WeMos_D1_Mini_OLED_Shield1.D6, WeMos_D1_Mini_OLED_Shield2.D6, R1.Pin_1, WeMos_D1_Mini1.D6
  N9: WeMos_D1_Mini_OLED_Shield1.D7, WeMos_D1_Mini_OLED_Shield2.D7, WeMos_D1_Mini1.D7
  N10: WeMos_D1_Mini_OLED_Shield1.D8, WeMos_D1_Mini_OLED_Shield2.D8, WeMos_D1_Mini1.D8, S8.Pin_1, S8.Pin_2
  N11: WeMos_D1_Mini_OLED_Shield1.RST, WeMos_D1_Mini_OLED_Shield2.RST, WeMos_D1_Mini1.RST
  N12: WeMos_D1_Mini_OLED_Shield1.RX, WeMos_D1_Mini_OLED_Shield2.RX, WeMos_D1_Mini1.RX
  N13: WeMos_D1_Mini_OLED_Shield1.TX, WeMos_D1_Mini_OLED_Shield2.TX, WeMos_D1_Mini1.TX
  N14: NEOPIXEL2.+5V, J4.pin3, J4.pin_6
  N15: NEOPIXEL2.DI, J4.pin2, J4.pin_5
  N16: NEOPIXEL2.GND, J4.pin1, J4.pin_4
  N17: J3.pin2, R6.Pin_1
  N18: S3.Pin_1, S3.Pin_2
  N19: S2.Pin_1, S2.Pin_2
  N20: S1.Pin_1, S1.Pin_2
  N21: S4.Pin_1, S4.Pin_2
  N22: S4.Pin_3, S4.Pin_4, R3.Pin_0
  N23: C2.+, U1.input_voltage, S6.O
  N24: BAT1.-, BAT3.+
  N25: BAT1.+, BAT2.-
  N26: J10.PWR, J10.tip_PWR, J11.PWR, J11.tip_PWR, S6.P, BAT6.-
  N27: BAT2.+, BAT7.-
  N28: BAT3.-, BAT5.+
  N29: S8.Pin_3, S8.Pin_4

custom parts:
  Neopixel Strip -- Black (60/m): Neopixel Strip, Black, 60 pixels per meter.
  Power Plug: Power Jack This is the standard 5.5mm barrel plug for power. This part has bendable leads (i.e. wires in the real world) to connect to wall warts or the breadboard in the standard wire end, and hidden connectors on the tip end that will connect when "plugged in" (overlapped with the jack so it appears "plugged in" in breadboard) to the modified coax jack part. Internal busses connect the two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
  Power Jack: Power Jack This is the standard 5.5mm barrel jack for power. Ths one is modified to mate with the barrel plug part and allow the two to "connect" so batteries and wall warts can be "connected" in breadboard and will go through to schematic.
  Pushbutton: A generic pushbutton. This is a standard 12mm square momentary button. What we really like is the large button head and good tactile feel (it ‘clicks’ really well). This button is great for user input on a PCB or a good, big reset button on a breadboard. Breadboard friendly! SparkFun Storefront SKU: COM-09190 Modified by: Ho Yun "Bobby" Chan @ SparkFun Electronics Inc.
